# Fritzing sketch project1Diagram (saved by Fritzing 0.9.3b)
breadboards: 1

parts:
  hc-sr1 = hc-sr04
  hc-sr2 = hc-sr04  # not connected
  Part1 = Arduino Uno (Rev3)

nets:
  GND: hc-sr1.GND, Part1.GND
